# Fritzing sketch attiny85 (saved by Fritzing 0.9.3b)
circuit board: 8.46667cm x 5.64444cm
breadboards: 1

parts:
  U1 = attiny85 [package=dip]
  R2 = Resistor [tolerance=±5% resistance=220 package=THT]
  R3 = Resistor [tolerance=±5% resistance=220 package=THT]
  LED2 = LED - 3mm [color="Yellow (595nm)" package="3 mm [THT]"]
  R1 = Resistor [tolerance=±5% resistance=220 package=THT]
  VCC1 = Battery
  LED3 = LED - 3mm [color="Green (555nm)" package="3 mm [THT]"]
  LED1 = LED - 3mm [color="Red (633nm)" package="3 mm [THT]"]

nets:
  N1: U1.Pin_4, LED2.cathode, VCC1.-, LED3.cathode, LED1.cathode
  N2: U1.Pin_5, R3.Pin_0
  N3: U1.Pin_6, R2.Pin_0
  N4: U1.Pin_7, R1.Pin_0
  N5: U1.Pin_8, VCC1.+
  N6: R2.Pin_1, LED2.anode
  N7: R3.Pin_1, LED3.anode
  N8: R1.Pin_1, LED1.anode
